// Logisim project 16bit-register.circ as structural Verilog: 1 circuit, main circuit main
module main (
  input  Clear,
  input  LOAD,
  input  INCREMENT,
  input  DECREMENT,
  input  I0,
  input  I1,
  input  I2,
  input  I3,
  input  I4,
  input  I5,
  input  I6,
  input  I7,
  input  I8,
  input  I9,
  input  I10,
  input  I11,
  input  I12,
  input  I13,
  input  I14,
  input  I15,
  output Overflow,
  output complement
);

  wire and_1_out, and_2_out, and_3_out, and_4_out, and_5_out, and_6_out, and_7_out, and_8_out, and_9_out,
       and_10_out, and_11_out, and_12_out, and_13_out, and_14_out, and_15_out, and_16_out, and_17_out,
       and_18_out, and_19_out, and_20_out, and_21_out, and_22_out, and_23_out, and_24_out, and_25_out,
       and_26_out, and_27_out, and_28_out, and_29_out, and_30_out, and_31_out, and_32_out, and_33_out,
       and_34_out, and_35_out, and_36_out, and_37_out, and_38_out, and_39_out, and_40_out, and_41_out,
       and_42_out, and_43_out, and_44_out, and_45_out, and_46_out, and_47_out, and_48_out, and_49_out,
       and_51_out, and_52_out, and_53_out, and_54_out, and_55_out, and_56_out, and_57_out, and_58_out,
       and_59_out, and_60_out, and_61_out, and_62_out, and_63_out, and_64_out, and_65_out, and_66_out,
       clock_1_out, JKff0_q, JKff0_qn, jkff1_q, jkff1_qn, jkff2_q, jkff2_qn, jkff3_q, jkff3_qn, jkff4_q,
       jkff4_qn, jkff5_q, jkff5_qn, jkff6_q, jkff6_qn, jkff7_q, jkff7_qn, jkff8_q, jkff8_qn, jkff9_q,
       jkff9_qn, jkff10_q, jkff10_qn, jkff11_q, jkff11_qn, jkff12_q, jkff12_qn, jkff13_q, jkff13_qn,
       jkff14_q, jkff14_qn, jkff15_q, jkff15_qn, not_1_out, not_2_out, not_3_out, not_5_out, not_6_out,
       not_7_out, not_8_out, not_9_out, not_10_out, not_11_out, not_12_out, not_13_out, not_14_out,
       not_15_out, not_16_out, not_17_out, not_18_out, not_19_out, not_20_out, or_1_out, or_2_out, or_3_out,
       or_4_out, or_5_out, or_6_out, or_7_out, or_8_out, or_9_out, or_10_out, or_11_out, or_12_out,
       or_13_out, or_14_out, or_15_out, or_16_out, or_17_out, or_18_out, or_19_out, or_20_out, or_21_out,
       or_22_out, or_23_out, or_24_out, or_25_out, or_26_out, or_27_out, or_28_out, or_29_out, or_30_out,
       or_31_out, or_32_out;

  Clock clock_1 (.out(clock_1_out));
  not not_1 (not_1_out, Clear);
  not not_2 (not_2_out, LOAD);
  not not_3 (not_3_out, INCREMENT);
  // NOT_Gate not_4 has open pins: in=DECREMENT, out=open
  not not_5 (not_5_out, I0);
  not not_6 (not_6_out, I1);
  not not_7 (not_7_out, I2);
  not not_8 (not_8_out, I3);
  not not_9 (not_9_out, I4);
  not not_10 (not_10_out, I5);
  not not_11 (not_11_out, I6);
  not not_12 (not_12_out, I7);
  not not_13 (not_13_out, I8);
  not not_14 (not_14_out, I9);
  not not_15 (not_15_out, I10);
  not not_16 (not_16_out, I11);
  not not_17 (not_17_out, I12);
  not not_18 (not_18_out, I13);
  not not_19 (not_19_out, I14);
  not not_20 (not_20_out, I15);
  and and_1 (and_1_out, not_1_out, LOAD);
  and and_2 (and_2_out, not_1_out, not_2_out, INCREMENT);
  and and_3 (and_3_out, and_1_out, I0);
  and and_4 (and_4_out, and_1_out, not_5_out);
  and and_5 (and_5_out, and_2_out, JKff0_q);
  and and_6 (and_6_out, and_1_out, I1);
  and and_7 (and_7_out, and_1_out, not_6_out);
  and and_8 (and_8_out, and_5_out, jkff1_q);
  and and_9 (and_9_out, and_1_out, I2);
  and and_10 (and_10_out, and_1_out, not_7_out);
  and and_11 (and_11_out, and_8_out, jkff2_q);
  and and_12 (and_12_out, and_1_out, I3);
  and and_13 (and_13_out, and_1_out, not_8_out);
  and and_14 (and_14_out, and_11_out, jkff3_q);
  and and_15 (and_15_out, and_1_out, I4);
  and and_16 (and_16_out, and_1_out, not_9_out);
  and and_17 (and_17_out, and_14_out, jkff4_q);
  and and_18 (and_18_out, and_1_out, I5);
  and and_19 (and_19_out, and_1_out, not_10_out);
  and and_20 (and_20_out, and_17_out, jkff5_q);
  and and_21 (and_21_out, and_1_out, I6);
  and and_22 (and_22_out, and_1_out, not_11_out);
  and and_23 (and_23_out, and_20_out, jkff6_q);
  and and_24 (and_24_out, and_1_out, I7);
  and and_25 (and_25_out, and_1_out, not_12_out);
  and and_26 (and_26_out, and_23_out, jkff7_q);
  and and_27 (and_27_out, and_1_out, I8);
  and and_28 (and_28_out, and_1_out, not_13_out);
  and and_29 (and_29_out, and_26_out, jkff8_q);
  and and_30 (and_30_out, and_1_out, I9);
  and and_31 (and_31_out, and_1_out, not_14_out);
  and and_32 (and_32_out, and_29_out, jkff9_q);
  and and_33 (and_33_out, and_1_out, I10);
  and and_34 (and_34_out, and_1_out, not_15_out);
  and and_35 (and_35_out, and_32_out, jkff10_q);
  and and_36 (and_36_out, and_1_out, I11);
  and and_37 (and_37_out, and_1_out, not_16_out);
  and and_38 (and_38_out, and_35_out, jkff11_q);
  and and_39 (and_39_out, and_1_out, I12);
  and and_40 (and_40_out, and_1_out, not_17_out);
  and and_41 (and_41_out, and_38_out, jkff12_q);
  and and_42 (and_42_out, and_1_out, I13);
  and and_43 (and_43_out, and_1_out, not_18_out);
  and and_44 (and_44_out, and_41_out, jkff13_q);
  and and_45 (and_45_out, and_1_out, I14);
  and and_46 (and_46_out, and_1_out, not_19_out);
  and and_47 (and_47_out, and_44_out, jkff14_q);
  and and_48 (and_48_out, and_1_out, I15);
  and and_49 (and_49_out, and_1_out, not_20_out);
  and and_50 (Overflow, and_47_out, jkff15_q);
  and and_51 (and_51_out, not_1_out, not_2_out, not_3_out, DECREMENT);
  and and_52 (and_52_out, and_51_out, JKff0_qn);
  and and_53 (and_53_out, and_52_out, jkff1_qn);
  and and_54 (and_54_out, and_53_out, jkff2_qn);
  and and_55 (and_55_out, and_54_out, jkff3_qn);
  and and_56 (and_56_out, and_55_out, jkff4_qn);
  and and_57 (and_57_out, and_56_out, jkff5_qn);
  and and_58 (and_58_out, and_57_out, jkff6_qn);
  and and_59 (and_59_out, and_58_out, jkff7_qn);
  and and_60 (and_60_out, and_59_out, jkff8_qn);
  and and_61 (and_61_out, and_60_out, jkff9_qn);
  and and_62 (and_62_out, and_61_out, jkff10_qn);
  and and_63 (and_63_out, and_62_out, jkff11_qn, jkff11_qn);
  and and_64 (and_64_out, and_63_out, jkff12_qn);
  and and_65 (and_65_out, and_64_out, jkff13_qn);
  and and_66 (and_66_out, and_65_out, jkff14_qn, jkff14_qn);
  and and_67 (complement, and_66_out, jkff15_qn);
  or or_1 (or_1_out, and_2_out, and_51_out, and_3_out);
  or or_2 (or_2_out, and_2_out, and_51_out, Clear, and_4_out);
  or or_3 (or_3_out, and_5_out, and_52_out, and_6_out);
  or or_4 (or_4_out, Clear, and_52_out, and_5_out, and_7_out);
  or or_5 (or_5_out, and_8_out, and_53_out, and_9_out);
  or or_6 (or_6_out, and_8_out, Clear, and_53_out, and_10_out);
  or or_7 (or_7_out, and_11_out, and_54_out, and_12_out);
  or or_8 (or_8_out, and_11_out, and_54_out, Clear, and_13_out);
  or or_9 (or_9_out, and_14_out, and_55_out, and_15_out);
  or or_10 (or_10_out, and_14_out, Clear, and_55_out, and_16_out);
  or or_11 (or_11_out, and_56_out, and_17_out, and_18_out);
  or or_12 (or_12_out, and_17_out, Clear, and_56_out, and_19_out);
  or or_13 (or_13_out, and_20_out, and_57_out, and_21_out);
  or or_14 (or_14_out, and_20_out, Clear, and_57_out, and_22_out);
  or or_15 (or_15_out, and_23_out, and_58_out, and_24_out);
  or or_16 (or_16_out, and_23_out, Clear, and_58_out, and_25_out);
  or or_17 (or_17_out, and_59_out, and_26_out, and_27_out);
  or or_18 (or_18_out, and_26_out, Clear, and_59_out, and_28_out);
  or or_19 (or_19_out, and_29_out, and_60_out, and_30_out);
  or or_20 (or_20_out, and_29_out, Clear, and_60_out, and_31_out);
  or or_21 (or_21_out, and_32_out, and_61_out, and_33_out);
  or or_22 (or_22_out, and_32_out, Clear, and_61_out, and_34_out);
  or or_23 (or_23_out, and_35_out, and_62_out, and_36_out);
  or or_24 (or_24_out, and_35_out, Clear, and_62_out, and_37_out);
  or or_25 (or_25_out, and_38_out, and_63_out, and_39_out);
  or or_26 (or_26_out, and_38_out, Clear, and_63_out, and_40_out);
  or or_27 (or_27_out, and_41_out, and_64_out, and_42_out);
  or or_28 (or_28_out, and_41_out, Clear, and_64_out, and_43_out);
  or or_29 (or_29_out, and_44_out, and_65_out, and_45_out);
  or or_30 (or_30_out, and_44_out, Clear, and_65_out, and_46_out);
  or or_31 (or_31_out, and_47_out, and_66_out, and_48_out);
  or or_32 (or_32_out, and_47_out, Clear, and_66_out, and_49_out);
  J_K_Flip_Flop JKff0 (
    .J(or_1_out), .clk(clock_1_out), .K(or_2_out), .Q(JKff0_q), .Qn(JKff0_qn));  // open: preset, en, reset
  J_K_Flip_Flop jkff1 (
    .J(or_3_out), .clk(clock_1_out), .K(or_4_out), .Q(jkff1_q), .Qn(jkff1_qn));  // open: preset, en, reset
  J_K_Flip_Flop jkff2 (
    .J(or_5_out), .clk(clock_1_out), .K(or_6_out), .Q(jkff2_q), .Qn(jkff2_qn));  // open: preset, en, reset
  J_K_Flip_Flop jkff3 (
    .J(or_7_out), .clk(clock_1_out), .K(or_8_out), .Q(jkff3_q), .Qn(jkff3_qn));  // open: preset, en, reset
  J_K_Flip_Flop jkff4 (
    .J(or_9_out), .clk(clock_1_out), .K(or_10_out), .Q(jkff4_q), .Qn(jkff4_qn));  // open: preset, en, reset
  J_K_Flip_Flop jkff5 (
    .J(or_11_out), .clk(clock_1_out), .K(or_12_out), .Q(jkff5_q), .Qn(jkff5_qn));  // open: preset, en, reset
  J_K_Flip_Flop jkff6 (
    .J(or_13_out), .clk(clock_1_out), .K(or_14_out), .Q(jkff6_q), .Qn(jkff6_qn));  // open: preset, en, reset
  J_K_Flip_Flop jkff7 (
    .J(or_15_out), .clk(clock_1_out), .K(or_16_out), .Q(jkff7_q), .Qn(jkff7_qn));  // open: preset, en, reset
  J_K_Flip_Flop jkff8 (
    .J(or_17_out), .clk(clock_1_out), .K(or_18_out), .Q(jkff8_q), .Qn(jkff8_qn));  // open: preset, en, reset
  J_K_Flip_Flop jkff9 (
    .J(or_19_out), .clk(clock_1_out), .K(or_20_out), .Q(jkff9_q), .Qn(jkff9_qn));  // open: preset, en, reset
  J_K_Flip_Flop jkff10 (
    .J(or_21_out), .clk(clock_1_out), .K(or_22_out), .Q(jkff10_q), .Qn(jkff10_qn));  // open: preset, en, reset
  J_K_Flip_Flop jkff11 (
    .J(or_23_out), .clk(clock_1_out), .K(or_24_out), .Q(jkff11_q), .Qn(jkff11_qn));  // open: preset, en, reset
  J_K_Flip_Flop jkff12 (
    .J(or_25_out), .clk(clock_1_out), .K(or_26_out), .Q(jkff12_q), .Qn(jkff12_qn));  // open: preset, en, reset
  J_K_Flip_Flop jkff13 (
    .J(or_27_out), .clk(clock_1_out), .K(or_28_out), .Q(jkff13_q), .Qn(jkff13_qn));  // open: preset, en, reset
  J_K_Flip_Flop jkff14 (
    .J(or_29_out), .clk(clock_1_out), .K(or_30_out), .Q(jkff14_q), .Qn(jkff14_qn));  // open: preset, en, reset
  J_K_Flip_Flop jkff15 (
    .J(or_31_out), .clk(clock_1_out), .K(or_32_out), .Q(jkff15_q), .Qn(jkff15_qn));  // open: preset, en, reset

  // Notes on the sheet:
  //   load
  //   increment
  //   decrement
  //   L*I
  //   L*I'
  //   CLEAR
  //   ınc
  //   clr
  //   L*I+INC(P)+DEC(P')
  //   L*I'+INC(P)+C+DEC(P')
endmodule
