// Logisim project assocCache.circ as structural Verilog: 1 circuit, main circuit main
module main (
  input  [4:0] in_1,
  input  in_2,
  input  [7:0] Data_load,
  input  [3:0] tag_load,
  output Hit
);

  wire and_1_out, and_2_out, and_3_out, and_4_out, and_5_out, and_6_out, and_7_out, and_8_out, and_9_out,
       and_10_out, and_11_out, and_12_out, and_13_out, and_14_out, and_15_out, and_16_out, button_1_out,
       button_2_out, button_3_out, button_4_out, button_5_out, button_6_out, button_7_out, button_8_out,
       button_9_out, button_10_out, button_11_out, button_12_out, button_13_out, button_14_out,
       button_15_out, button_16_out, button_17_out, button_18_out, button_19_out, button_20_out,
       button_21_out, button_22_out, button_23_out, button_24_out, clock_1_out, comparator_1_eq,
       comparator_2_eq, comparator_3_eq, comparator_4_eq, comparator_5_eq, comparator_6_eq, comparator_7_eq,
       comparator_8_eq, d_ff_1_q, not_1_out;
  wire [3:0] controlled_buffer_1_out, register_1_q, register_2_q, register_3_q, register_4_q, register_5_q,
       register_6_q, register_7_q, register_8_q, register_9_q, register_10_q, register_11_q, register_12_q,
       register_13_q, register_14_q, register_15_q, register_16_q, register_17_q, register_18_q,
       register_19_q, register_20_q, register_21_q, register_22_q, register_23_q, register_24_q;

  Clock clock_1 (.out(clock_1_out));
  not not_1 (not_1_out, in_1[4]);
  D_Flip_Flop d_ff_1 (.clk(clock_1_out), .D(in_2), .Q(d_ff_1_q));  // open: Qn, preset, en, reset
  Register #(.width(4)) register_1 (.D(tag_load), .Q(register_1_q), .clk(button_1_out));  // open: en, clr
  Button button_1 (.out(button_1_out));
  Register #(.width(4)) register_2 (.D(tag_load), .Q(register_2_q), .clk(button_2_out));  // open: en, clr
  Button button_2 (.out(button_2_out));
  Register #(.width(4)) register_3 (.D(tag_load), .Q(register_3_q), .clk(button_3_out));  // open: en, clr
  Button button_3 (.out(button_3_out));
  Register #(.width(4)) register_4 (.D(tag_load), .Q(register_4_q), .clk(button_4_out));  // open: en, clr
  Button button_4 (.out(button_4_out));
  Register #(.width(4)) register_5 (.D(tag_load), .Q(register_5_q), .clk(button_5_out));  // open: en, clr
  Button button_5 (.out(button_5_out));
  Register #(.width(4)) register_6 (.D(tag_load), .Q(register_6_q), .clk(button_6_out));  // open: en, clr
  Button button_6 (.out(button_6_out));
  Register #(.width(4)) register_7 (.D(tag_load), .Q(register_7_q), .clk(button_7_out));  // open: en, clr
  Button button_7 (.out(button_7_out));
  Register #(.width(4)) register_8 (.D(tag_load), .Q(register_8_q), .clk(button_8_out));  // open: en, clr
  Button button_8 (.out(button_8_out));
  // Probe on comparator_1_eq
  Comparator #(.width(4)) comparator_1 (.a(register_1_q), .b(in_1[3:0]), .eq(comparator_1_eq));  // open: gt, lt
  // Probe on comparator_2_eq
  Comparator #(.width(4)) comparator_2 (.a(register_2_q), .b(in_1[3:0]), .eq(comparator_2_eq));  // open: gt, lt
  // Probe on comparator_3_eq
  Comparator #(.width(4)) comparator_3 (.a(register_3_q), .b(in_1[3:0]), .eq(comparator_3_eq));  // open: gt, lt
  // Probe on comparator_4_eq
  Comparator #(.width(4)) comparator_4 (.a(register_4_q), .b(in_1[3:0]), .eq(comparator_4_eq));  // open: gt, lt
  // Probe on comparator_5_eq
  Comparator #(.width(4)) comparator_5 (.a(register_5_q), .b(in_1[3:0]), .eq(comparator_5_eq));  // open: gt, lt
  // Probe on comparator_6_eq
  Comparator #(.width(4)) comparator_6 (.a(register_6_q), .b(in_1[3:0]), .eq(comparator_6_eq));  // open: gt, lt
  // Probe on comparator_7_eq
  Comparator #(.width(4)) comparator_7 (.a(register_7_q), .b(in_1[3:0]), .eq(comparator_7_eq));  // open: gt, lt
  // Probe on comparator_8_eq
  Comparator #(.width(4)) comparator_8 (.a(register_8_q), .b(in_1[3:0]), .eq(comparator_8_eq));  // open: gt, lt
  and and_1 (and_1_out, comparator_1_eq, d_ff_1_q, in_1[4]);
  and and_2 (and_2_out, comparator_1_eq, not_1_out, d_ff_1_q);
  and and_3 (and_3_out, comparator_2_eq, d_ff_1_q, in_1[4]);
  and and_4 (and_4_out, comparator_2_eq, d_ff_1_q, not_1_out);
  and and_5 (and_5_out, comparator_3_eq, d_ff_1_q, in_1[4]);
  and and_6 (and_6_out, comparator_3_eq, d_ff_1_q, not_1_out);
  and and_7 (and_7_out, comparator_4_eq, d_ff_1_q, in_1[4]);
  and and_8 (and_8_out, comparator_4_eq, d_ff_1_q, not_1_out);
  and and_9 (and_9_out, comparator_5_eq, d_ff_1_q, in_1[4]);
  and and_10 (and_10_out, comparator_5_eq, d_ff_1_q, not_1_out);
  and and_11 (and_11_out, comparator_6_eq, d_ff_1_q, in_1[4]);
  and and_12 (and_12_out, comparator_6_eq, d_ff_1_q, not_1_out);
  and and_13 (and_13_out, comparator_7_eq, d_ff_1_q, in_1[4]);
  and and_14 (and_14_out, comparator_7_eq, d_ff_1_q, not_1_out);
  and and_15 (and_15_out, comparator_8_eq, d_ff_1_q, in_1[4]);
  and and_16 (and_16_out, comparator_8_eq, d_ff_1_q, not_1_out);
  Register #(.width(4)) register_9 (.D(Data_load[7:4]), .Q(register_9_q), .clk(button_9_out));  // open: en, clr
  assign controlled_buffer_1_out = and_1_out ? register_9_q : 4'bz;  // Controlled_Buffer controlled_buffer_1
  Button button_9 (.out(button_9_out));
  Register #(.width(4)) register_10 (.D(Data_load[7:4]), .Q(register_10_q), .clk(button_10_out));  // open: en, clr
  assign controlled_buffer_1_out = and_3_out ? register_10_q : 4'bz;  // Controlled_Buffer controlled_buffer_2
  Button button_10 (.out(button_10_out));
  assign controlled_buffer_1_out = and_5_out ? register_11_q : 4'bz;  // Controlled_Buffer controlled_buffer_3
  Register #(.width(4)) register_11 (.D(Data_load[7:4]), .Q(register_11_q), .clk(button_11_out));  // open: en, clr
  Button button_11 (.out(button_11_out));
  Register #(.width(4)) register_12 (.D(Data_load[7:4]), .Q(register_12_q), .clk(button_12_out));  // open: en, clr
  assign controlled_buffer_1_out = and_7_out ? register_12_q : 4'bz;  // Controlled_Buffer controlled_buffer_4
  Button button_12 (.out(button_12_out));
  Register #(.width(4)) register_13 (.D(Data_load[7:4]), .Q(register_13_q), .clk(button_13_out));  // open: en, clr
  assign controlled_buffer_1_out = and_9_out ? register_13_q : 4'bz;  // Controlled_Buffer controlled_buffer_5
  Button button_13 (.out(button_13_out));
  assign controlled_buffer_1_out = and_11_out ? register_14_q : 4'bz;  // Controlled_Buffer controlled_buffer_6
  Register #(.width(4)) register_14 (.D(Data_load[7:4]), .Q(register_14_q), .clk(button_14_out));  // open: en, clr
  Button button_14 (.out(button_14_out));
  Register #(.width(4)) register_15 (.D(Data_load[7:4]), .Q(register_15_q), .clk(button_15_out));  // open: en, clr
  assign controlled_buffer_1_out = and_13_out ? register_15_q : 4'bz;  // Controlled_Buffer controlled_buffer_7
  Button button_15 (.out(button_15_out));
  assign controlled_buffer_1_out = and_15_out ? register_16_q : 4'bz;  // Controlled_Buffer controlled_buffer_8
  Register #(.width(4)) register_16 (.D(Data_load[7:4]), .Q(register_16_q), .clk(button_16_out));  // open: en, clr
  Button button_16 (.out(button_16_out));
  Register #(.width(4)) register_17 (.D(Data_load[3:0]), .Q(register_17_q), .clk(button_17_out));  // open: en, clr
  assign controlled_buffer_1_out = and_2_out ? register_17_q : 4'bz;  // Controlled_Buffer controlled_buffer_9
  Button button_17 (.out(button_17_out));
  assign controlled_buffer_1_out = and_4_out ? register_18_q : 4'bz;  // Controlled_Buffer controlled_buffer_10
  Register #(.width(4)) register_18 (.D(Data_load[3:0]), .Q(register_18_q), .clk(button_18_out));  // open: en, clr
  Button button_18 (.out(button_18_out));
  assign controlled_buffer_1_out = and_6_out ? register_19_q : 4'bz;  // Controlled_Buffer controlled_buffer_11
  Register #(.width(4)) register_19 (.D(Data_load[3:0]), .Q(register_19_q), .clk(button_19_out));  // open: en, clr
  Button button_19 (.out(button_19_out));
  assign controlled_buffer_1_out = and_8_out ? register_20_q : 4'bz;  // Controlled_Buffer controlled_buffer_12
  Register #(.width(4)) register_20 (.D(Data_load[3:0]), .Q(register_20_q), .clk(button_20_out));  // open: en, clr
  Button button_20 (.out(button_20_out));
  Register #(.width(4)) register_21 (.D(Data_load[3:0]), .Q(register_21_q), .clk(button_21_out));  // open: en, clr
  assign controlled_buffer_1_out = and_10_out ? register_21_q : 4'bz;  // Controlled_Buffer controlled_buffer_13
  Button button_21 (.out(button_21_out));
  Register #(.width(4)) register_22 (.D(Data_load[3:0]), .Q(register_22_q), .clk(button_22_out));  // open: en, clr
  Controlled_Buffer #(.width(4)) controlled_buffer_14 (.in(register_22_q), .en(and_12_out));  // open: out
  Button button_22 (.out(button_22_out));
  assign controlled_buffer_1_out = and_14_out ? register_23_q : 4'bz;  // Controlled_Buffer controlled_buffer_15
  Register #(.width(4)) register_23 (.D(Data_load[3:0]), .Q(register_23_q), .clk(button_23_out));  // open: en, clr
  Button button_23 (.out(button_23_out));
  assign controlled_buffer_1_out = and_16_out ? register_24_q : 4'bz;  // Controlled_Buffer controlled_buffer_16
  Register #(.width(4)) register_24 (.D(Data_load[3:0]), .Q(register_24_q), .clk(button_24_out));  // open: en, clr
  Button button_24 (.out(button_24_out));
  // Probe on controlled_buffer_1_out
  or or_1 (Hit, comparator_1_eq, comparator_2_eq, comparator_3_eq, comparator_4_eq, comparator_5_eq, comparator_6_eq, comparator_7_eq, comparator_8_eq);

  // Notes on the sheet:
  //   Tag karsilastirma(XNOR ile de yapılabilirdi devrenin sadeliği açısından 4 bitlik comparator kullanılmıştır.)
  //   validity bit
  //   Validity hattı
  //   Bu biilgiye göre bütün rowlar aynı anda valid yada invalid olacaktır.(0 olunca data bus' a veri aktarılmaz)
  //   esasında her bir row için validity Flip Flop u olmalıdır, devrenin karmaşıklığını artırmaması açısından  Bütün rowlar aynı validty değeri ile beslenmiştir
  //   WORD 1
  //   word 0
  //   Yine devrenin sade gözükmesi için 4x3 = 12 ayrı flip flop yerine 3 adet D tipi 4bit-register ile devre tasarlanmıştır
endmodule
